# Fritzing sketch Untitled Sketch 2 (saved by Fritzing 0.9.3b)
breadboards: 1

parts:
  元件2 = Arduino Uno (Rev3)
  R5 = Resistor [tolerance=±5% resistance=220 package=THT]
  LED3 = LED - 5mm [color="Green (565nm)" package="5 mm [THT]"]
  LED4 = LED - 5mm [color="Red (633nm)" package="5 mm [THT]"]
  R6 = Resistor [tolerance=±5% resistance=220 package=THT]
  S5 = SWITCH-MOMENTARY-2 [package=tactile-pth-12mm]
  R7 = Resistor [tolerance=±5% resistance=220 package=THT]
  R8 = Resistor [tolerance=±5% resistance=220 package=THT]
  S6 = SWITCH-MOMENTARY-2 [package=tactile-pth-12mm]
  OMRON1 = OMRON PCB Power Relay – G5LE [part_number="G5LE-1\n" package=THT]
  J1 = Peltier Element

nets:
  N1: 元件2.D8, OMRON1.COIL2
  N2: 元件2.D9_PWM, S6.2
  N3: 元件2.D10_PWM/SS, S5.2
  N4: 元件2.D11_PWM/MOSI, LED3.cathode
  N5: 元件2.D12/MISO, LED4.cathode
  N6: 元件2.GND, OMRON1.COIL1, J1.pin1
  N7: 元件2.5V, OMRON1.A, OMRON1.C
  N8: R5.Pin_0, LED3.anode
  N9: R5.Pin_1, R6.Pin_1
  N10: LED4.anode, R6.Pin_0
  N11: S5.1, R7.Pin_0
  N12: R8.Pin_0, S6.1
  N13: OMRON1.B, J1.pin2
